// Logisim project final 7_Seg_Display (1).circ as structural Verilog: 4 circuits, main circuit main
module main (
  input  in_1,
  input  in_2,
  input  in_3,
  input  in_4,
  input  in_5
);

  wire alu_1_out_2, and_1_out, and_2_out, clock_1_out, n7_seg_driver_1_p5, n7_seg_driver_1_p6,
       n7_seg_driver_1_p7, n7_seg_driver_1_p8, n7_seg_driver_1_p9, n7_seg_driver_1_p10, n7_seg_driver_1_p11;
  wire [2:0] adder_1_out, register_1_q;
  wire [3:0] n7_seg_driver_1_p1, ram_1_data, rom_1_data;

  Clock clock_1 (.out(clock_1_out));
  and and_1 (and_1_out, clock_1_out, in_5);
  Register #(.width(3)) register_1 (.D(adder_1_out), .Q(register_1_q), .clk(and_1_out));  // open: en, clr
  Adder #(.width(3)) adder_1 (.a(3'b001), .b(register_1_q), .out(adder_1_out));  // open: cin, cout
  ROM #(.addrWidth(3), .dataWidth(4)) rom_1 (.addr(register_1_q), .data(rom_1_data));  // open: sel
  // _7_seg_Driver 7_seg_driver_1: pin names not known; wires that end beside it: n7_seg_driver_1_p1[0], n7_seg_driver_1_p1[1], n7_seg_driver_1_p1[2], n7_seg_driver_1_p1[3], n7_seg_driver_1_p5, n7_seg_driver_1_p6, n7_seg_driver_1_p7, n7_seg_driver_1_p8, n7_seg_driver_1_p9, n7_seg_driver_1_p10, n7_seg_driver_1_p11
  _7_Segment_Display u_7_segment_display_1 (
    .g(n7_seg_driver_1_p11), .f(n7_seg_driver_1_p10), .a(n7_seg_driver_1_p5), .b(n7_seg_driver_1_p6),
    .e(n7_seg_driver_1_p9), .d(n7_seg_driver_1_p8), .c(n7_seg_driver_1_p7));  // open: dp
  _4_bit_register u_4_bit_register_1 (.in_1(rom_1_data), .out_3(n7_seg_driver_1_p1));  // open: in_2
  ALU alu_1 (.in_1(rom_1_data), .out_2(alu_1_out_2));
  LED Extra_Turn (.in(alu_1_out_2));
  and and_2 (and_2_out, in_4, clock_1_out);
  RAM #(.addrWidth(4), .dataWidth(4), .bus("separate")) ram_1 (
    .addr(ram_1_data), .din(n7_seg_driver_1_p1), .data(ram_1_data), .str(in_1), .sel(in_2), .clk(and_2_out),
    .clr(in_3));  // open: ld

  // Notes on the sheet:
  //   GHULAM MUSTAFA BCPE223005
  //   contents of rom_1 (hex, n*v repeats v):
  //   0 1 2 3 4 5 6
  //   4 BIT CPU TO CONTROL DICE
  //   Dice Display
  //   MOHAMMAD UZAIR BCPE223049
endmodule

module _4_Bit_Counter (
  input  Enable,
  input  Clk,
  output B0,
  output B1,
  output B2,
  output B3,
  output Co
);

  wire and_1_out, and_2_out, and_3_out;

  Clock Clock ();  // open: out
  and and_1 (and_1_out, Enable, B0);
  and and_2 (and_2_out, and_1_out, B1);
  and and_3 (and_3_out, and_2_out, B2);
  J_K_Flip_Flop j_k_ff_1 (.J(Enable), .clk(Clk), .K(Enable), .Q(B0));  // open: Qn, preset, en, reset
  J_K_Flip_Flop j_k_ff_2 (.J(and_1_out), .clk(Clk), .K(and_1_out), .Q(B1));  // open: Qn, preset, en, reset
  J_K_Flip_Flop j_k_ff_3 (.J(and_2_out), .clk(Clk), .K(and_2_out), .Q(B2));  // open: Qn, preset, en, reset
  J_K_Flip_Flop j_k_ff_4 (.J(and_3_out), .clk(Clk), .K(and_3_out), .Q(B3));  // open: Qn, preset, en, reset
  and and_4 (Co, B3, and_3_out);
endmodule

module _4_bit_register (
  input  [3:0] in_1,
  input  in_2,
  output [3:0] out_3
);

  wire clock_1_out;

  Clock clock_1 (.out(clock_1_out));
  D_Flip_Flop d_ff_1 (.clk(clock_1_out), .D(in_1[3]), .Q(out_3[3]), .reset(in_2));  // open: Qn, preset, en
  D_Flip_Flop d_ff_2 (.clk(clock_1_out), .D(in_1[2]), .Q(out_3[2]), .reset(in_2));  // open: Qn, preset, en
  D_Flip_Flop d_ff_3 (.clk(clock_1_out), .D(in_1[1]), .Q(out_3[1]), .reset(in_2));  // open: Qn, preset, en
  D_Flip_Flop d_ff_4 (.clk(clock_1_out), .D(in_1[0]), .Q(out_3[0]), .reset(in_2));  // open: Qn, preset, en
endmodule

module ALU (
  input  [3:0] in_1,
  output out_2
);

  Comparator #(.width(4)) comparator_1 (.a(in_1), .b(4'b0110), .eq(out_2));  // open: gt, lt
endmodule
